# Fritzing sketch Final-product (saved by Fritzing 0.9.9b)
breadboards: 1

parts:
  Part1 = Arduino Uno (Rev3) - ICSP
  U1 = NodeMCU V1.0
  M1 = Dagu DGServo 9g (Top view) [part_number=RS001B]
  Keypad4x1 = Keypad Membran 4x4
  Mod1 = KY-012 Active Buzzer Module [package="Breakout board"]
  Part2 = BH1750FVI Breakout Board [part_number=BH1750FVI]  # not connected
  Mod2 = KY-008 Laser Transmitter Module [package="Breakout board"]

nets:
  N1: Part1.ICSP_MISO, Part1.D12/MISO, M1.pulse
  N2: Part1.ICSP_MOSI, Part1.D11_PWM/MOSI, Keypad4x1.Pin1
  N3: Part1.D8, Keypad4x1.Pin4
  N4: Part1.D9_PWM, Keypad4x1.Pin3
  N5: Part1.D10_PWM/SS, Keypad4x1.Pin2
  N6: Part1.D13/SCK, Mod1.S
  GND: Part1.GND, M1.gnd, Mod1.-
  N7: Part1.D2, U1.RX
  N8: Part1.D3_PWM, U1.TX
  N9: Part1.D4, Keypad4x1.Pin8
  N10: Part1.D5_PWM, Keypad4x1.Pin7
  N11: Part1.D6_PWM, Keypad4x1.Pin6
  N12: Part1.D7, Keypad4x1.Pin5
  3V3: Part1.3V3, M1.vcc
  N13: U1.GND, Mod2.-
  N14: U1.D5, Mod2.S

custom parts:
  NodeMCU V1.0: ESP8266 based NodeMCU
  Keypad Membran 4x4: Membrane Keypad 4x4 Matrix
  KY-012 Active Buzzer Module: Active Piezoelectric Buzzer Module KY-012, it produces single-tone sound when signal is high. (Special thanks to vanepp for fixing the PCB holes and other errors)
  BH1750FVI Breakout Board: The ROHM Semiconductor BH1750FVI is a digital ambient light sensor for the I2C bus interface. The BH750FVI is able to detect a wide range of light intensities (1-65535 lux). The spectral range is similar to that of the human eye.
  KY-008 Laser Transmitter Module: KY-008 Laser Transmitter Module, emits a dot shaped red laser beam.
