# Fritzing sketch KY-012-KY-008-BH1750-GY30 (saved by Fritzing 0.9.9b)
breadboards: 1

parts:
  Part1 = Arduino Uno (Rev3) - ICSP
  Mod1 = KY-008 Laser Transmitter Module [package="Breakout board"]
  Part3 = BH1750FVI Breakout Board [part_number=BH1750FVI]  # not connected
  Mod2 = KY-012 Active Buzzer Module [package="Breakout board"]
  M1 = ESP-01 Breakout Board Breadboard Adapter [part_number=ESP8266]

nets:
  N1: Part1.ICSP_MISO, Part1.D12/MISO, Mod1.S
  N2: Part1.D8, Mod2.S
  GND: Part1.GND, Mod1.-, Mod2.-, M1.GND
  3V3: Part1.3V3, M1.CHPD, M1.VCC

custom parts:
  KY-008 Laser Transmitter Module: KY-008 Laser Transmitter Module, emits a dot shaped red laser beam.
  BH1750FVI Breakout Board: The ROHM Semiconductor BH1750FVI is a digital ambient light sensor for the I2C bus interface. The BH750FVI is able to detect a wide range of light intensities (1-65535 lux). The spectral range is similar to that of the human eye.
  KY-012 Active Buzzer Module: Active Piezoelectric Buzzer Module KY-012, it produces single-tone sound when signal is high. (Special thanks to vanepp for fixing the PCB holes and other errors)
  ESP-01 Breakout Board Breadboard Adapter: Generic WiFi Module based on the ESP8266 with onboard PCB antenna and UART communications with breadboard friendly breakout board attached.
