# Fritzing sketch main (saved by Fritzing 0.9.9b)
breadboards: 1

parts:
  Part1 = Arduino Uno (Rev3) - ICSP
  M1 = ESP-01 Breakout Board Breadboard Adapter [part_number=ESP8266]
  Mod1 = KY-012 Active Buzzer Module [package="Breakout board"]
  Mod2 = KY-008 Laser Transmitter Module [package="Breakout board"]
  Part2 = BH1750FVI Breakout Board [part_number=BH1750FVI]  # not connected

nets:
  N1: Part1.D8, Mod1.S
  GND: Part1.GND, M1.GND, Mod1.-, Mod2.-
  N2: Part1.D0/RX, M1.TXD
  N3: Part1.D1/TX, M1.RXD
  N4: Part1.D7, Mod2.S
  3V3: Part1.3V3, M1.CHPD, M1.VCC

custom parts:
  ESP-01 Breakout Board Breadboard Adapter: Generic WiFi Module based on the ESP8266 with onboard PCB antenna and UART communications with breadboard friendly breakout board attached.
  KY-012 Active Buzzer Module: Active Piezoelectric Buzzer Module KY-012, it produces single-tone sound when signal is high. (Special thanks to vanepp for fixing the PCB holes and other errors)
  KY-008 Laser Transmitter Module: KY-008 Laser Transmitter Module, emits a dot shaped red laser beam.
  BH1750FVI Breakout Board: The ROHM Semiconductor BH1750FVI is a digital ambient light sensor for the I2C bus interface. The BH750FVI is able to detect a wide range of light intensities (1-65535 lux). The spectral range is similar to that of the human eye.
